// Logisim project MultiCycleMips.circ as structural Verilog: 7 circuits, main circuit Main
module Main (
);

  wire alu_1_zero, and_1_out, and_2_out, Clock, comparator_1_eq, comparator_2_eq, control_1_alusrca,
       control_1_iord, control_1_irwrite, control_1_jr, control_1_pcwrite, control_1_pcwritecond,
       control_1_regwrite, ld, lw_sw, or_1_out, str;
  wire [1:0] control_1_aluop, control_1_alusrcb, control_1_memtoreg, control_1_pcsrc, control_1_regdst;
  wire [2:0] aluctrl_1_aluctrl;
  wire [3:0] register_1_q_2;
  wire [4:0] WriteAddr;
  wire [5:0] _0_5;
  wire [7:0] multiplexer_1_out;
  wire [25:6] MAR_q;
  wire [27:0] bit_extender_2_out, register_1_q, shifter_2_out;
  wire [31:0] adder_1_out, alu_1_aluresult, bit_extender_1_out, MDR_q, multiplexer_2_out, multiplexer_4_out,
       multiplexer_5_out, multiplexer_6_out, multiplexer_7_out, ram_1_data, register_2_q, register_3_q,
       register_4_q, register_file_1_rddata1, register_file_1_rddata2, shifter_1_out;
  wire [31:26] MAR_q_2;

  Clock clock_1 (.out(Clock));
  // Probe on {register_1_q_2, register_1_q}
  Register #(.width(32)) register_1 (
    .D(multiplexer_7_out), .en(or_1_out), .Q({register_1_q_2, register_1_q}), .clk(Clock));  // open: clr
  // Probe on and_1_out
  or or_1 (or_1_out, and_1_out, control_1_pcwrite);
  Multiplexer #(.width(8), .enable("false")) multiplexer_1 (
    .in0(register_1_q[9:2]), .in1(multiplexer_6_out[7:0]), .out(multiplexer_1_out), .sel(control_1_iord));
  and and_1 (and_1_out, alu_1_zero, control_1_pcwritecond);
  // Probe on str
  // Probe on MDR_q
  RAM #(.dataWidth(32), .bus("separate")) ram_1 (
    .addr(multiplexer_1_out), .din(register_3_q), .data(ram_1_data), .str(str), .clk(Clock), .ld(ld));  // open: sel, clr
  Register #(.width(32)) MDR (.D(ram_1_data), .Q(MDR_q), .clk(Clock));  // open: en, clr
  Register #(.width(32)) MAR (
    .D(ram_1_data), .en(control_1_irwrite), .Q({MAR_q_2, MAR_q, _0_5}), .clk(Clock));  // open: clr
  Control control_1 (
    .PCWriteCond(control_1_pcwritecond), .PCWrite(control_1_pcwrite), .IorD(control_1_iord), .MemRead(ld),
    .Memwrite(str), .MemtoReg(control_1_memtoreg), .IRWrite(control_1_irwrite), .Func(_0_5), .Clock(Clock),
    .Opcode(MAR_q_2), .PCSrc(control_1_pcsrc), .ALUOp(control_1_aluop), .ALUSrcB(control_1_alusrcb),
    .ALUSrcA(control_1_alusrca), .RegWrite(control_1_regwrite), .RegDst(control_1_regdst), .JR(control_1_jr));
  // Probe on control_1_jr
  Multiplexer #(.select(2), .width(32), .enable("false")) multiplexer_2 (
    .in0(MDR_q), .in1(multiplexer_6_out), .in2({register_1_q_2, register_1_q}), .out(multiplexer_2_out),
    .sel(control_1_memtoreg));  // open: in3
  Multiplexer #(.select(2), .width(5), .enable("false")) multiplexer_3 (
    .in0(MAR_q[20:16]), .in1(MAR_q[15:11]), .in2({5{1'b1}}), .out(WriteAddr), .sel(control_1_regdst));  // open: in3
  // Probe on WriteAddr
  // Probe on control_1_regwrite
  // Probe on multiplexer_2_out
  Comparator #(.width(6)) comparator_1 (.a(6'b101011), .b(MAR_q_2), .eq(comparator_1_eq));  // open: gt, lt
  Comparator #(.width(6)) comparator_2 (.a(6'b100011), .b(MAR_q_2), .eq(comparator_2_eq));  // open: gt, lt
  Register_File register_file_1 (
    .WrAddr(WriteAddr), .WrData(multiplexer_2_out), .WrReg(control_1_regwrite), .RdAddr1(MAR_q[25:21]),
    .RdAddr2(MAR_q[20:16]), .RdData1(register_file_1_rddata1), .RdData2(register_file_1_rddata2),
    .Clock(Clock));
  assign bit_extender_1_out = {{16{MAR_q[15]}}, {MAR_q[15:6], _0_5}};  // Bit_Extender bit_extender_1
  or or_2 (lw_sw, comparator_1_eq, comparator_2_eq);
  assign bit_extender_2_out = {{2{1'b0}}, {MAR_q, _0_5}};  // Bit_Extender bit_extender_2
  Register #(.width(32)) register_2 (.D(register_file_1_rddata1), .Q(register_2_q), .clk(Clock));  // open: en, clr
  Register #(.width(32)) register_3 (.D(register_file_1_rddata2), .Q(register_3_q), .clk(Clock));  // open: en, clr
  Shifter #(.width(32)) shifter_1 (.in(bit_extender_1_out), .\dist (5'b00010), .out(shifter_1_out));
  Multiplexer #(.width(32), .enable("false")) multiplexer_4 (
    .in0({register_1_q_2, register_1_q}), .in1(register_2_q), .out(multiplexer_4_out), .sel(control_1_alusrca));
  Multiplexer #(.select(2), .width(32), .enable("false")) multiplexer_5 (
    .in0(register_3_q), .in1(32'h4), .in2(bit_extender_1_out), .in3(shifter_1_out), .out(multiplexer_5_out),
    .sel(control_1_alusrcb));
  Shifter #(.width(28)) shifter_2 (.in(bit_extender_2_out), .\dist (5'b00010), .out(shifter_2_out));
  AluCtrl aluctrl_1 (.OPc(MAR_q_2), .Func(_0_5), .ALUOp(control_1_aluop), .ALUCtrl(aluctrl_1_aluctrl));
  ALU alu_1 (
    .ALUCtl(aluctrl_1_aluctrl), .A(multiplexer_4_out), .B(multiplexer_5_out), .ALUResult(alu_1_aluresult),
    .Zero(alu_1_zero), .Shamt(MAR_q[10:6]));  // open: Overflow
  Register #(.width(32)) register_4 (.D(alu_1_aluresult), .Q(register_4_q), .clk(Clock));  // open: en, clr
  Multiplexer #(.width(32), .enable("false")) multiplexer_6 (
    .in0(register_4_q), .in1(adder_1_out), .out(multiplexer_6_out), .sel(lw_sw));
  Multiplexer #(.select(2), .width(32), .enable("false")) multiplexer_7 (
    .in0(alu_1_aluresult), .in1(register_4_q), .in2({register_1_q_2, shifter_2_out}),
    .out(multiplexer_7_out), .sel(control_1_pcsrc));  // open: in3
  // Probe on control_1_pcsrc[1]
  and and_2 (and_2_out, control_1_regwrite, control_1_pcsrc[1]);
  // Probe on and_2_out
  Adder #(.width(32)) adder_1 (.a(register_4_q), .b(32'h80), .out(adder_1_out));  // open: cin, cout
endmodule

module _32_Bit_Adder___Subtractor (
  input  Add_Sub_control,
  input  [31:0] in_2,
  input  [31:0] in_3,
  output [31:0] out_4,
  output carry_out
);

  wire adder_1_cout, subtractor_1_bout;
  wire [31:0] adder_1_out, subtractor_1_out;

  Adder #(.width(32)) adder_1 (.a(in_2), .b(in_3), .out(adder_1_out), .cout(adder_1_cout));  // open: cin
  Subtractor #(.width(32)) subtractor_1 (
    .a(in_2), .b(in_3), .out(subtractor_1_out), .bout(subtractor_1_bout));  // open: bin
  Multiplexer #(.width(32), .enable("false")) multiplexer_1 (
    .in0(adder_1_out), .in1(subtractor_1_out), .out(out_4), .sel(Add_Sub_control));
  Multiplexer #(.enable("false")) multiplexer_2 (
    .in0(adder_1_cout), .in1(subtractor_1_bout), .out(carry_out), .sel(Add_Sub_control));
endmodule

module ALU (
  input  [2:0] ALUCtl,
  input  [31:0] A,
  input  [31:0] B,
  input  [4:0] Shamt,
  output [31:0] ALUResult,
  output Zero,
  output Overflow
);

  wire and_2_out, and_3_out, comparator_1_lt, not_1_out, not_2_out, or_2_out;
  wire [31:0] Add, And, LessThan, Nor, Or, ShiftLeft, ShiftRight, Sub, Xor;

  // Probe on ALUCtl
  assign Nor = ~(A | B);  // NOR_Gate nor_1, 32 bits wide
  Adder #(.width(32)) adder_1 (.a(A), .b(B), .out(Add));  // open: cin, cout
  Subtractor #(.width(32)) subtractor_1 (.a(A), .b(B), .out(Sub));  // open: bin, bout
  assign And = A & B;  // AND_Gate and_1, 32 bits wide
  assign Or = A | B;  // OR_Gate or_1, 32 bits wide
  assign Xor = A ^ B;  // XOR_Gate xor_1, 32 bits wide
  Comparator #(.width(32)) comparator_1 (.a(A), .b(B), .lt(comparator_1_lt));  // open: gt, eq
  assign LessThan = {{31{1'b0}}, comparator_1_lt};  // Bit_Extender bit_extender_1
  Shifter #(.width(32)) shifter_1 (.in(B), .\dist (Shamt), .out(ShiftLeft));
  Shifter #(.width(32), .shift("lr")) shifter_2 (.in(B), .\dist (Shamt), .out(ShiftRight));
  Multiplexer #(.select(3), .width(32), .enable("false")) multiplexer_1 (
    .in0(And), .in1(Add), .in2(Or), .in3(Sub), .in4(LessThan), .in5(Xor), .in6(ShiftRight), .in7(ShiftLeft),
    .out(ALUResult), .sel(ALUCtl));
  not not_1 (not_1_out, ALUCtl[1]);
  not not_2 (not_2_out, ALUCtl[2]);
  and and_2 (and_2_out, ALUCtl[0], not_1_out, not_2_out);
  and and_3 (and_3_out, ALUCtl[0], ALUCtl[1], not_2_out);
  Overflow overflow_1 (
    .Add(and_2_out), .Sub(and_3_out), .ASign(A[31]), .BSign(B[31]), .ResultSign(ALUResult[31]),
    .Overflow(Overflow));
  or or_2 (or_2_out, ALUResult[0], ALUResult[1], ALUResult[2], ALUResult[3], ALUResult[4], ALUResult[5], ALUResult[6], ALUResult[7], ALUResult[8], ALUResult[9], ALUResult[10], ALUResult[11], ALUResult[12], ALUResult[13], ALUResult[14], ALUResult[15], ALUResult[16], ALUResult[17], ALUResult[18], ALUResult[19], ALUResult[20], ALUResult[21], ALUResult[22], ALUResult[23], ALUResult[24], ALUResult[25], ALUResult[26], ALUResult[27], ALUResult[28], ALUResult[29], ALUResult[30], ALUResult[31]);
  not not_3 (Zero, or_2_out);

  // Other names for the same wires on the sheet: ASign = A[31]; ResultSign = ALUResult[31]; BSign = B[31]
endmodule

module Register_File (
  input  [4:0] WrAddr,
  input  [31:0] WrData,
  input  WrReg,
  input  [4:0] RdAddr1,
  input  [4:0] RdAddr2,
  input  Clock,
  output [31:0] RdData1,
  output [31:0] RdData2
);

  wire WrReg0, WrReg1, WrReg2, WrReg3, WrReg4, WrReg5, WrReg6, WrReg7, WrReg8, WrReg9, WrReg10, WrReg11,
       WrReg12, WrReg13, WrReg14, WrReg15, WrReg16, WrReg17, WrReg18, WrReg19, WrReg20, WrReg21, WrReg22,
       WrReg23, WrReg24, WrReg25, WrReg26, WrReg27, WrReg28, WrReg29, WrReg30, WrReg31;
  wire [31:0] RegData1, RegData2, RegData3, RegData4, RegData5, RegData6, RegData7, RegData8, RegData9,
       RegData10, RegData11, RegData12, RegData13, RegData14, RegData15, RegData16, RegData17, RegData18,
       RegData19, RegData20, RegData21, RegData22, RegData23, RegData24, RegData25, RegData26, RegData27,
       RegData28, RegData29, RegData30, RegData31;

  Demultiplexer #(.select(5), .enable("false")) demultiplexer_1 (
    .out0(WrReg0), .out1(WrReg1), .out2(WrReg2), .out3(WrReg3), .out4(WrReg4), .out5(WrReg5), .out6(WrReg6),
    .out7(WrReg7), .out8(WrReg8), .out9(WrReg9), .out10(WrReg10), .out11(WrReg11), .out12(WrReg12),
    .out13(WrReg13), .out14(WrReg14), .out15(WrReg15), .out16(WrReg16), .out17(WrReg17), .out18(WrReg18),
    .out19(WrReg19), .out20(WrReg20), .out21(WrReg21), .out22(WrReg22), .out23(WrReg23), .out24(WrReg24),
    .out25(WrReg25), .out26(WrReg26), .out27(WrReg27), .out28(WrReg28), .out29(WrReg29), .out30(WrReg30),
    .out31(WrReg31), .in(WrReg), .sel(WrAddr));
  Register #(.width(32)) Reg4 (.D(WrData), .en(WrReg4), .Q(RegData4), .clk(Clock));  // open: clr
  Register #(.width(32)) Reg8 (.D(WrData), .en(WrReg8), .Q(RegData8), .clk(Clock));  // open: clr
  Register #(.width(32)) Reg12 (.D(WrData), .en(WrReg12), .Q(RegData12), .clk(Clock));  // open: clr
  Register #(.width(32)) Reg16 (.D(WrData), .en(WrReg16), .Q(RegData16), .clk(Clock));  // open: clr
  Register #(.width(32)) Reg20 (.D(WrData), .en(WrReg20), .Q(RegData20), .clk(Clock));  // open: clr
  Register #(.width(32)) Reg24 (.D(WrData), .en(WrReg24), .Q(RegData24), .clk(Clock));  // open: clr
  Register #(.width(32)) Reg28 (.D(WrData), .en(WrReg28), .Q(RegData28), .clk(Clock));  // open: clr
  Register #(.width(32)) Reg1 (.D(WrData), .en(WrReg1), .Q(RegData1), .clk(Clock));  // open: clr
  Register #(.width(32)) Reg5 (.D(WrData), .en(WrReg5), .Q(RegData5), .clk(Clock));  // open: clr
  Register #(.width(32)) Reg9 (.D(WrData), .en(WrReg9), .Q(RegData9), .clk(Clock));  // open: clr
  Register #(.width(32)) Reg13 (.D(WrData), .en(WrReg13), .Q(RegData13), .clk(Clock));  // open: clr
  Register #(.width(32)) Reg17 (.D(WrData), .en(WrReg17), .Q(RegData17), .clk(Clock));  // open: clr
  Register #(.width(32)) Reg21 (.D(WrData), .en(WrReg21), .Q(RegData21), .clk(Clock));  // open: clr
  Register #(.width(32)) Reg25 (.D(WrData), .en(WrReg25), .Q(RegData25), .clk(Clock));  // open: clr
  Register #(.width(32)) Reg29 (.D(WrData), .en(WrReg29), .Q(RegData29), .clk(Clock));  // open: clr
  Register #(.width(32)) Reg2 (.D(WrData), .en(WrReg2), .Q(RegData2), .clk(Clock));  // open: clr
  Register #(.width(32)) Reg6 (.D(WrData), .en(WrReg6), .Q(RegData6), .clk(Clock));  // open: clr
  Register #(.width(32)) Reg10 (.D(WrData), .en(WrReg10), .Q(RegData10), .clk(Clock));  // open: clr
  Register #(.width(32)) Reg14 (.D(WrData), .en(WrReg14), .Q(RegData14), .clk(Clock));  // open: clr
  Register #(.width(32)) Reg18 (.D(WrData), .en(WrReg18), .Q(RegData18), .clk(Clock));  // open: clr
  Register #(.width(32)) Reg22 (.D(WrData), .en(WrReg22), .Q(RegData22), .clk(Clock));  // open: clr
  Register #(.width(32)) Reg26 (.D(WrData), .en(WrReg26), .Q(RegData26), .clk(Clock));  // open: clr
  Register #(.width(32)) Reg30 (.D(WrData), .en(WrReg30), .Q(RegData30), .clk(Clock));  // open: clr
  Register #(.width(32)) Reg3 (.D(WrData), .en(WrReg3), .Q(RegData3), .clk(Clock));  // open: clr
  Register #(.width(32)) Reg7 (.D(WrData), .en(WrReg7), .Q(RegData7), .clk(Clock));  // open: clr
  Register #(.width(32)) Reg11 (.D(WrData), .en(WrReg11), .Q(RegData11), .clk(Clock));  // open: clr
  Register #(.width(32)) Reg15 (.D(WrData), .en(WrReg15), .Q(RegData15), .clk(Clock));  // open: clr
  Register #(.width(32)) Reg19 (.D(WrData), .en(WrReg19), .Q(RegData19), .clk(Clock));  // open: clr
  Register #(.width(32)) Reg23 (.D(WrData), .en(WrReg23), .Q(RegData23), .clk(Clock));  // open: clr
  Register #(.width(32)) Reg27 (.D(WrData), .en(WrReg27), .Q(RegData27), .clk(Clock));  // open: clr
  Register #(.width(32)) Reg31 (.D(WrData), .en(WrReg31), .Q(RegData31), .clk(Clock));  // open: clr
  Multiplexer #(.select(5), .width(32), .enable("false")) multiplexer_1 (
    .in0({32{1'b0}}), .in1(RegData1), .in2(RegData2), .in3(RegData3), .in4(RegData4), .in5(RegData5),
    .in6(RegData6), .in7(RegData7), .in8(RegData8), .in9(RegData9), .in10(RegData10), .in11(RegData11),
    .in12(RegData12), .in13(RegData13), .in14(RegData14), .in15(RegData15), .in16(RegData16),
    .in17(RegData17), .in18(RegData18), .in19(RegData19), .in20(RegData20), .in21(RegData21),
    .in22(RegData22), .in23(RegData23), .in24(RegData24), .in25(RegData25), .in26(RegData26),
    .in27(RegData27), .in28(RegData28), .in29(RegData29), .in30(RegData30), .in31(RegData31), .out(RdData1),
    .sel(RdAddr1));
  Multiplexer #(.select(5), .width(32), .enable("false")) multiplexer_2 (
    .in0({32{1'b0}}), .in1(RegData1), .in2(RegData2), .in3(RegData3), .in4(RegData4), .in5(RegData5),
    .in6(RegData6), .in7(RegData7), .in8(RegData8), .in9(RegData9), .in10(RegData10), .in11(RegData11),
    .in12(RegData12), .in13(RegData13), .in14(RegData14), .in15(RegData15), .in16(RegData16),
    .in17(RegData17), .in18(RegData18), .in19(RegData19), .in20(RegData20), .in21(RegData21),
    .in22(RegData22), .in23(RegData23), .in24(RegData24), .in25(RegData25), .in26(RegData26),
    .in27(RegData27), .in28(RegData28), .in29(RegData29), .in30(RegData30), .in31(RegData31), .out(RdData2),
    .sel(RdAddr2));
endmodule

module Overflow (
  input  Add,
  input  Sub,
  input  ASign,
  input  BSign,
  input  ResultSign,
  output Overflow
);

  wire and_1_out, and_2_out, or_1_out, xnor_1_out, xor_1_out, xor_2_out;

  xnor xnor_1 (xnor_1_out, ASign, BSign);
  xor xor_1 (xor_1_out, ASign, BSign);
  and and_1 (and_1_out, xnor_1_out, Add);
  and and_2 (and_2_out, xor_1_out, Sub);
  or or_1 (or_1_out, and_1_out, and_2_out);
  xor xor_2 (xor_2_out, ResultSign, ASign);
  and and_3 (Overflow, or_1_out, xor_2_out);

  // Notes on the sheet:
  //   Overflow occurs when doing addition and sign(A) == sign(B) && sign(result) != sign(A)
  //   Or
  //   Overflow occurs when doing subtraction and sign(A) != sign(B) && sign(result) != sign(A)
endmodule

module Control (
  input  Clock,
  input  [5:0] Opcode,
  input  [5:0] Func,
  output [1:0] PCSrc,
  output PCWriteCond,
  output PCWrite,
  output [1:0] ALUOp,
  output IorD,
  output [1:0] ALUSrcB,
  output MemRead,
  output ALUSrcA,
  output Memwrite,
  output RegWrite,
  output [1:0] MemtoReg,
  output IRWrite,
  output [1:0] RegDst,
  output JR
);

  wire comparator_1_eq, comparator_2_eq, comparator_3_eq;
  wire [3:0] JrcheckState, register_1_q;
  wire [21:4] rom_1_data;

  Register #(.width(4), .trigger("falling")) register_1 (
    .D(JrcheckState), .Q(register_1_q), .clk(Clock));  // open: en, clr
  Comparator #(.width(4)) comparator_1 (.a(4'b0111), .b(JrcheckState), .eq(comparator_1_eq));  // open: gt, lt
  ROM #(.addrWidth(10), .dataWidth(22)) rom_1 (
    .addr({Opcode, register_1_q}), .data({rom_1_data, JrcheckState}));  // open: sel
  Comparator #(.width(6)) comparator_2 (.a({6{1'b0}}), .b(Opcode), .eq(comparator_2_eq));  // open: gt, lt
  Comparator #(.width(6)) comparator_3 (.a(6'b001000), .b(Func), .eq(comparator_3_eq));  // open: gt, lt
  Multiplexer #(.width(18), .enable("false")) multiplexer_1 (
    .in0(rom_1_data), .in1(18'h20008),
    .out({PCWrite, PCWriteCond, IorD, MemRead, Memwrite, IRWrite, MemtoReg, PCSrc, ALUOp, ALUSrcB, ALUSrcA, RegWrite, RegDst}),
    .sel(JR));
  and and_1 (JR, comparator_2_eq, comparator_1_eq, comparator_3_eq);

  // Other names for the same wires on the sheet: JRR = JR

  // Notes on the sheet:
  //   contents of rom_1 (hex, n*v repeats v):
  //   250101 6 4*0 887 4050 8*0 250101 30a 8*0 202000 5*0 250101 30a 8*0 202000 5*0 250101 206 4*0 8 0
  //   1160e0 7*0 250101 309 7*0 101480 6*0 250101 15*0 250101 15*0 250101 15*0 250101 206 4*0 287 4040 8*0
  //   250101 15*0 250101 15*0 250101 15*0 250101 206 4*0 a87 4040 8*0 250101 206 4*0 a87 4040 8*0 250101
  //   15*0 250101 15*0 250101 15*0 250101 15*0 250101 15*0 250101 15*0 250101 15*0 250101 15*0 250101 15*0
  //   250101 15*0 250101 15*0 250101 15*0 250101 15*0 250101 15*0 250101 15*0 250101 15*0 250101 15*0
  //   250101 15*0 250101 15*0 250101 15*0 250101 15*0 250101 302 283 c0004 40 11*0 250101 15*0 250101 15*0
  //   250101 15*0 250101 15*0 250101 15*0 250101 15*0 250101 15*0 250101 302 285 0 0 a0000 10*0 250101
  //   15*0 250101 15*0 250101 15*0 250101 15*0 250101 15*0 250101 15*0 250101 15*0 250101 15*0 250101 15*0
  //   250101 15*0 250101 15*0 250101 15*0 250101 15*0 250101 15*0 250101 15*0 250101 15*0 250101 15*0
  //   250101 15*0 250101 15*0 250101
endmodule

module AluCtrl (
  input  [1:0] ALUOp,
  input  [5:0] OPc,
  input  [5:0] Func,
  output [2:0] ALUCtrl
);

  wire and_1_out, and_2_out, and_3_out, and_4_out, and_5_out, and_6_out, and_7_out, and_9_out, not_1_out,
       or_1_out, or_2_out, or_3_out, or_4_out, or_5_out;
  wire [1:0] undriven_2;
  wire [2:0] or_6_out;
  wire [3:0] undriven;
  wire [5:0] multiplexer_1_out, rom_1_data;

  ROM #(.addrWidth(6), .dataWidth(6)) rom_1 (.addr(OPc), .data(rom_1_data));  // open: sel
  or or_1 (or_1_out, OPc[0], OPc[1], OPc[2], OPc[3], OPc[4], OPc[5]);
  not not_1 (not_1_out, or_1_out);
  Multiplexer #(.width(6), .enable("false")) multiplexer_1 (
    .in0(rom_1_data), .in1(Func), .out(multiplexer_1_out), .sel(not_1_out));
  and and_1 (and_1_out, ~undriven[1], ~undriven[2]);  // AND_Gate
  and and_2 (and_2_out, undriven[1], undriven[2]);
  ROM #(.dataWidth(3)) rom_2 (.addr({ALUOp, multiplexer_1_out}), .data(ALUCtrl));  // open: sel
  or or_2 (or_2_out, undriven[1], ~undriven[2]);  // OR_Gate
  or or_3 (or_3_out, undriven[0], ~undriven[2]);  // OR_Gate
  and and_3 (and_3_out, ~undriven[3], or_4_out);  // AND_Gate
  or or_4 (or_4_out, and_1_out, and_2_out);
  and and_4 (and_4_out, ~undriven[0], or_2_out);  // AND_Gate
  and and_5 (and_5_out, or_3_out, ~undriven[3]);  // AND_Gate
  or or_5 (or_5_out, ~undriven_2[0], undriven_2[0]);  // OR_Gate
  and and_6 (and_6_out, or_5_out, ~undriven_2[1]);  // AND_Gate
  and and_7 (and_7_out, undriven_2[1], and_3_out);
  and and_8 (or_6_out[2], undriven_2[1], and_4_out);
  and and_9 (and_9_out, undriven_2[1], and_5_out);
  or or_6 (or_6_out[0], and_6_out, and_7_out);
  or or_7 (or_6_out[1], undriven_2[0], and_9_out);

  // Notes on the sheet:
  //   contents of rom_1 (hex, n*v repeats v):
  //   8*0 20 0 0 0 24 25
  //   contents of rom_2 (hex, n*v repeats v):
  //   64*1 64*3 7 0 6 29*0 1 0 3 0 0 2 5 0 0 0 4
endmodule
