// Logisim project MultiCycleMipsHazard.circ as structural Verilog: 12 circuits, main circuit Main
module Main (
);

  wire Clk, comparator_1_eq, control_1_branch, control_1_jal, decode_reg_1_memout, hazardu_1_flushe,
       hazardu_1_forwardad, hazardu_1_forwardbd, hazardu_1_stalld, hazardu_1_stallf, MemWrite, not_1_out,
       or_1_out, RegWriteW;
  wire [1:0] and_1_out, control_1_wr, decode_reg_1_wrtout, hazardu_1_forwardae, hazardu_1_forwardbe,
       RegWriteM;
  wire [1:1] mem_reg_1_writeback_2;
  wire [2:2] control_1_mm;
  wire [4:0] control_1_ex, decode_reg_1_destout, decode_reg_1_exeout, decode_reg_1_shamtout,
       decode_reg_1_srcout, decode_reg_1_tgtout, execute_reg_1_writereg_2, multiplexer_3_out,
       multiplexer_7_out, Read_1, Read_2, WriteAddr;
  wire [7:0] multiplexer_4_out;
  wire [27:0] bit_extender_2_out, fetchreg_1_outpc;
  wire [31:0] adder_1_out, adder_2_out, alu_1_aluresult, bit_extender_1_out, decode_reg_1_immout,
       decode_reg_1_rd1out, decode_reg_1_rd2out, execute_reg_1_aluout_2, execute_reg_1_writedata_2,
       fetchreg_1_outinst, FwdE_M, FwdM_W, mem_reg_1_aluout_2, mem_reg_1_readdata_2, multiplexer_1_out,
       multiplexer_2_out, multiplexer_8_out, multiplexer_10_out, PC_q, ram_1_data, register_file_1_rddata1,
       register_file_1_rddata2, rom_1_data, shifter_1_out, shifter_2_out, Vla;

  Clock clock_1 (.out(Clk));
  Multiplexer #(.select(2), .width(32), .enable("false")) multiplexer_1 (
    .in0(adder_1_out), .in1(adder_2_out), .in2(shifter_2_out), .out(multiplexer_1_out), .sel(and_1_out));  // open: in3
  HazardU hazardu_1 (
    .RegSrcD(Read_1), .RegTargetD(Read_2), .RegSrcE(decode_reg_1_srcout), .RegTargetE(decode_reg_1_tgtout),
    .WriteRegW(WriteAddr), .StallF(hazardu_1_stallf), .StallD(hazardu_1_stalld), .FlushE(hazardu_1_flushe),
    .ForwardAD(hazardu_1_forwardad), .ForwardBD(hazardu_1_forwardbd), .ForwardAE(hazardu_1_forwardae),
    .ForwardBE(hazardu_1_forwardbe), .MemtoRegE(decode_reg_1_memout), .RegWriteW(RegWriteW),
    .RegWriteM(RegWriteM[0]), .WriteRegM(execute_reg_1_writereg_2));  // open: WriteRegE, BranchD, JumpD, RegWriteE, MemtoRegM
  Register #(.width(32)) PC (.D(multiplexer_1_out), .en(hazardu_1_stallf), .Q(PC_q), .clk(Clk));  // open: clr
  Adder #(.width(32)) adder_1 (.a(PC_q), .b(32'h4), .out(adder_1_out));  // open: cin, cout
  ROM #(.dataWidth(32)) rom_1 (.addr(PC_q[9:2]), .data(rom_1_data));  // open: sel
  or or_1 (or_1_out, and_1_out[0], and_1_out[1]);
  FetchReg fetchreg_1 (
    .InInst(rom_1_data), .InPC(adder_1_out),
    .OutInst({fetchreg_1_outinst[31:26], Read_1, Read_2, fetchreg_1_outinst[15:0]}),
    .OutPC({shifter_2_out[31:28], fetchreg_1_outpc}), .Clock(Clk), .clear(hazardu_1_stalld), .Stall(or_1_out));
  Multiplexer #(.width(32), .enable("false")) multiplexer_2 (
    .in0(FwdM_W), .in1({shifter_2_out[31:28], fetchreg_1_outpc}), .out(multiplexer_2_out), .sel(control_1_jal));
  Multiplexer #(.width(5), .enable("false")) multiplexer_3 (
    .in0(WriteAddr), .in1({5{1'b1}}), .out(multiplexer_3_out), .sel(control_1_jal));
  assign bit_extender_1_out = {{16{fetchreg_1_outinst[15]}}, fetchreg_1_outinst[15:0]};  // Bit_Extender bit_extender_1
  assign bit_extender_2_out = {{2{1'b0}}, {Read_1, Read_2, fetchreg_1_outinst[15:0]}};  // Bit_Extender bit_extender_2
  Control control_1 (
    .Op(fetchreg_1_outinst[31:26]), .Func(fetchreg_1_outinst[5:0]), .WR(control_1_wr), .MM(control_1_mm[2]),
    .EX(control_1_ex), .Jal(control_1_jal), .Branch(control_1_branch), .Jump(and_1_out[1]));
  Register_File register_file_1 (
    .WrAddr(multiplexer_3_out), .WrData(multiplexer_2_out), .WrReg(RegWriteW), .RdAddr1(Read_1),
    .RdAddr2(Read_2), .RdData1(register_file_1_rddata1), .RdData2(register_file_1_rddata2), .Clock(Clk));
  Shifter #(.width(32)) shifter_1 (.in(bit_extender_1_out), .\dist (5'b00010), .out(shifter_1_out));
  Shifter #(.width(28)) shifter_2 (.in(bit_extender_2_out), .\dist (5'b00010), .out(shifter_2_out[27:0]));
  and and_1 (and_1_out[0], control_1_branch, comparator_1_eq);
  Adder #(.width(32)) adder_2 (
    .a(shifter_1_out), .b({shifter_2_out[31:28], fetchreg_1_outpc}), .out(adder_2_out));  // open: cin, cout
  Multiplexer #(.width(8), .enable("false")) multiplexer_4 (
    .in0({control_1_ex, control_1_mm[2], control_1_wr}), .in1({8{1'b0}}), .out(multiplexer_4_out),
    .sel(hazardu_1_flushe));
  Multiplexer #(.width(32), .enable("false")) multiplexer_5 (.sel(hazardu_1_forwardad));  // open: in0, in1, out
  Multiplexer #(.width(32), .enable("false")) multiplexer_6 (.sel(hazardu_1_forwardbd));  // open: in0, in1, out
  Decode_Reg decode_reg_1 (
    .WrtCtrl(multiplexer_4_out[1:0]), .MemCtrl(multiplexer_4_out[2]), .ExeCtrl(multiplexer_4_out[7:3]),
    .Read_Data_1(register_file_1_rddata1), .Read_Data_2(register_file_1_rddata2),
    .Immediate(bit_extender_1_out), .Source(Read_1), .Target(Read_2), .Dest(fetchreg_1_outinst[15:11]),
    .WrtOut(decode_reg_1_wrtout), .MemOut(decode_reg_1_memout), .ExeOut(decode_reg_1_exeout),
    .RD1Out(decode_reg_1_rd1out), .RD2Out(decode_reg_1_rd2out), .ImmOut(decode_reg_1_immout),
    .SrcOut(decode_reg_1_srcout), .TgtOut(decode_reg_1_tgtout), .DestOut(decode_reg_1_destout), .clock(Clk),
    .ShamtOut(decode_reg_1_shamtout), .Shamt(fetchreg_1_outinst[10:6]));  // open: clear
  Comparator #(.width(32)) comparator_1 (
    .a(register_file_1_rddata1), .b(register_file_1_rddata2), .eq(comparator_1_eq));  // open: gt, lt
  Multiplexer #(.width(5), .enable("false")) multiplexer_7 (
    .in0(decode_reg_1_tgtout), .in1(decode_reg_1_destout), .out(multiplexer_7_out),
    .sel(decode_reg_1_exeout[4]));
  Multiplexer #(.select(2), .width(32), .enable("false")) multiplexer_8 (
    .in0(decode_reg_1_rd1out), .in1(FwdE_M), .in2(FwdM_W), .out(multiplexer_8_out), .sel(hazardu_1_forwardae));  // open: in3
  Multiplexer #(.select(2), .width(32), .enable("false")) multiplexer_9 (
    .in0(decode_reg_1_rd2out), .in1(FwdE_M), .in2(FwdM_W), .out(Vla), .sel(hazardu_1_forwardbe));  // open: in3
  Multiplexer #(.width(32), .enable("false")) multiplexer_10 (
    .in0(Vla), .in1(decode_reg_1_immout), .out(multiplexer_10_out), .sel(decode_reg_1_exeout[3]));
  ALU alu_1 (
    .ALUCtl(decode_reg_1_exeout[2:0]), .A(multiplexer_8_out), .B(multiplexer_10_out),
    .ALUResult(alu_1_aluresult), .Shamt(decode_reg_1_shamtout));  // open: Zero, Overflow
  Execute_Reg execute_reg_1 (
    .Writeback(decode_reg_1_wrtout), .Memory(decode_reg_1_memout), .AluOut(alu_1_aluresult), .WriteData(Vla),
    .WriteReg(multiplexer_7_out), .WriteBack_2(RegWriteM), .Memory_2(MemWrite),
    .AluOut_2(execute_reg_1_aluout_2), .WriteData_2(execute_reg_1_writedata_2),
    .WriteReg_2(execute_reg_1_writereg_2), .clock(Clk));
  Multiplexer #(.width(32), .enable("false")) multiplexer_11 (
    .in0(ram_1_data), .in1(execute_reg_1_aluout_2), .out(FwdE_M), .sel(RegWriteM[1]));
  not not_1 (not_1_out, MemWrite);
  Mem_Reg mem_reg_1 (
    .Writeback(RegWriteM), .ReadData(ram_1_data), .AluOut(execute_reg_1_aluout_2),
    .WriteReg(execute_reg_1_writereg_2), .WriteBack_2({mem_reg_1_writeback_2[1], RegWriteW}),
    .ReadData_2(mem_reg_1_readdata_2), .AluOut_2(mem_reg_1_aluout_2), .WriteReg_2(WriteAddr), .clock(Clk));
  RAM #(.dataWidth(32), .bus("separate")) ram_1 (
    .addr(execute_reg_1_aluout_2[7:0]), .din(execute_reg_1_writedata_2), .data(ram_1_data), .str(MemWrite),
    .clk(Clk), .ld(not_1_out));  // open: sel, clr
  Multiplexer #(.width(32), .enable("false")) multiplexer_12 (
    .in0(mem_reg_1_readdata_2), .in1(mem_reg_1_aluout_2), .out(FwdM_W), .sel(mem_reg_1_writeback_2[1]));
  // Probe on nothing
  // Probe on nothing
  // Probe on nothing
  // Probe on nothing
  // Probe on nothing
  // Probe on nothing
  // Probe on nothing
  // Probe on nothing
  // Probe on nothing
  // Probe on nothing

  // Other names for the same wires on the sheet: WriteData[31:0] = FwdM_W

  // Notes on the sheet:
  //   contents of rom_1 (hex, n*v repeats v):
  //   34010001 211020 221826 2064000e 232824 aca4000b 8ca6000b c43824 10e10003 c7402a 11080001 201cffff
  //   20090001 8c0a000c ad4a0013 8c0a000c 1141fffb c000013 201bffff 23ff0018 ac1f0000 8c0b0000 1600008
  //   201affff 8000018 2019ffff 2018ffff
endmodule

module _32_Bit_Adder___Subtractor (
  input  Add_Sub_control,
  input  [31:0] in_2,
  input  [31:0] in_3,
  output [31:0] out_4,
  output carry_out
);

  wire adder_1_cout, subtractor_1_bout;
  wire [31:0] adder_1_out, subtractor_1_out;

  Adder #(.width(32)) adder_1 (.a(in_2), .b(in_3), .out(adder_1_out), .cout(adder_1_cout));  // open: cin
  Subtractor #(.width(32)) subtractor_1 (
    .a(in_2), .b(in_3), .out(subtractor_1_out), .bout(subtractor_1_bout));  // open: bin
  Multiplexer #(.width(32), .enable("false")) multiplexer_1 (
    .in0(adder_1_out), .in1(subtractor_1_out), .out(out_4), .sel(Add_Sub_control));
  Multiplexer #(.enable("false")) multiplexer_2 (
    .in0(adder_1_cout), .in1(subtractor_1_bout), .out(carry_out), .sel(Add_Sub_control));
endmodule

module ALU (
  input  [2:0] ALUCtl,
  input  [31:0] A,
  input  [31:0] B,
  input  [4:0] Shamt,
  output [31:0] ALUResult,
  output Zero,
  output Overflow
);

  wire and_2_out, and_3_out, comparator_1_lt, not_1_out, not_2_out, or_2_out;
  wire [31:0] Add, And, LessThan, Nor, Or, ShiftLeft, ShiftRight, Sub, Xor;

  assign Xor = A ^ B;  // XOR_Gate xor_1, 32 bits wide
  Adder #(.width(32)) adder_1 (.a(A), .b(B), .out(Add));  // open: cin, cout
  Subtractor #(.width(32)) subtractor_1 (.a(A), .b(B), .out(Sub));  // open: bin, bout
  assign And = A & B;  // AND_Gate and_1, 32 bits wide
  assign Or = A | B;  // OR_Gate or_1, 32 bits wide
  assign Nor = ~(A | B);  // NOR_Gate nor_1, 32 bits wide
  Comparator #(.width(32)) comparator_1 (.a(A), .b(B), .lt(comparator_1_lt));  // open: gt, eq
  assign LessThan = {{31{1'b0}}, comparator_1_lt};  // Bit_Extender bit_extender_1
  Shifter #(.width(32)) shifter_1 (.in(B), .\dist (Shamt), .out(ShiftLeft));
  Shifter #(.width(32), .shift("lr")) shifter_2 (.in(B), .\dist (Shamt), .out(ShiftRight));
  not not_1 (not_1_out, ALUCtl[1]);
  not not_2 (not_2_out, ALUCtl[2]);
  Multiplexer #(.select(3), .width(32), .enable("false")) multiplexer_1 (
    .in0(And), .in1(Add), .in2(Or), .in3(Sub), .in4(LessThan), .in5(Xor), .in6(ShiftRight), .in7(ShiftLeft),
    .out(ALUResult), .sel(ALUCtl));
  and and_2 (and_2_out, ALUCtl[0], not_1_out, not_2_out);
  and and_3 (and_3_out, ALUCtl[0], ALUCtl[1], not_2_out);
  Overflow_Unit overflow_unit_1 (
    .Add(and_2_out), .Sub(and_3_out), .ASign(A[31]), .BSign(B[31]), .ResultSign(ALUResult[31]),
    .Overflow(Overflow));
  not not_3 (Zero, or_2_out);
  or or_2 (or_2_out, ALUResult[0], ALUResult[1], ALUResult[2], ALUResult[3], ALUResult[4], ALUResult[5], ALUResult[6], ALUResult[7], ALUResult[8], ALUResult[9], ALUResult[10], ALUResult[11], ALUResult[12], ALUResult[13], ALUResult[14], ALUResult[15], ALUResult[16], ALUResult[17], ALUResult[18], ALUResult[19], ALUResult[20], ALUResult[21], ALUResult[22], ALUResult[23], ALUResult[24], ALUResult[25], ALUResult[26], ALUResult[27], ALUResult[28], ALUResult[29], ALUResult[30], ALUResult[31]);

  // Other names for the same wires on the sheet: ASign = A[31]; ResultSign = ALUResult[31]; BSign = B[31]
endmodule

module Register_File (
  input  [4:0] WrAddr,
  input  [31:0] WrData,
  input  WrReg,
  input  [4:0] RdAddr1,
  input  [4:0] RdAddr2,
  input  Clock,
  output [31:0] RdData1,
  output [31:0] RdData2
);

  wire and_1_out, and_2_out, comparator_1_eq, comparator_2_eq, comparator_3_eq, comparator_4_eq, not_1_out,
       not_2_out, WrReg0, WrReg1, WrReg2, WrReg3, WrReg4, WrReg5, WrReg6, WrReg7, WrReg8, WrReg9, WrReg10,
       WrReg11, WrReg12, WrReg13, WrReg14, WrReg15, WrReg16, WrReg17, WrReg18, WrReg19, WrReg20, WrReg21,
       WrReg22, WrReg23, WrReg24, WrReg25, WrReg26, WrReg27, WrReg28, WrReg29, WrReg30, WrReg31;
  wire [31:0] multiplexer_1_out, multiplexer_2_out, RegData1, RegData2, RegData3, RegData4, RegData5,
       RegData6, RegData7, RegData8, RegData9, RegData10, RegData11, RegData12, RegData13, RegData14,
       RegData15, RegData16, RegData17, RegData18, RegData19, RegData20, RegData21, RegData22, RegData23,
       RegData24, RegData25, RegData26, RegData27, RegData28, RegData29, RegData30, RegData31;

  Demultiplexer #(.select(5), .enable("false")) demultiplexer_1 (
    .out0(WrReg0), .out1(WrReg1), .out2(WrReg2), .out3(WrReg3), .out4(WrReg4), .out5(WrReg5), .out6(WrReg6),
    .out7(WrReg7), .out8(WrReg8), .out9(WrReg9), .out10(WrReg10), .out11(WrReg11), .out12(WrReg12),
    .out13(WrReg13), .out14(WrReg14), .out15(WrReg15), .out16(WrReg16), .out17(WrReg17), .out18(WrReg18),
    .out19(WrReg19), .out20(WrReg20), .out21(WrReg21), .out22(WrReg22), .out23(WrReg23), .out24(WrReg24),
    .out25(WrReg25), .out26(WrReg26), .out27(WrReg27), .out28(WrReg28), .out29(WrReg29), .out30(WrReg30),
    .out31(WrReg31), .in(WrReg), .sel(WrAddr));
  Register #(.width(32)) Reg4 (.D(WrData), .en(WrReg4), .Q(RegData4), .clk(Clock));  // open: clr
  Register #(.width(32)) Reg8 (.D(WrData), .en(WrReg8), .Q(RegData8), .clk(Clock));  // open: clr
  Register #(.width(32)) Reg12 (.D(WrData), .en(WrReg12), .Q(RegData12), .clk(Clock));  // open: clr
  Register #(.width(32)) Reg16 (.D(WrData), .en(WrReg16), .Q(RegData16), .clk(Clock));  // open: clr
  Register #(.width(32)) Reg20 (.D(WrData), .en(WrReg20), .Q(RegData20), .clk(Clock));  // open: clr
  Register #(.width(32)) Reg24 (.D(WrData), .en(WrReg24), .Q(RegData24), .clk(Clock));  // open: clr
  Register #(.width(32)) Reg28 (.D(WrData), .en(WrReg28), .Q(RegData28), .clk(Clock));  // open: clr
  Register #(.width(32)) Reg1 (.D(WrData), .en(WrReg1), .Q(RegData1), .clk(Clock));  // open: clr
  Register #(.width(32)) Reg5 (.D(WrData), .en(WrReg5), .Q(RegData5), .clk(Clock));  // open: clr
  Register #(.width(32)) Reg9 (.D(WrData), .en(WrReg9), .Q(RegData9), .clk(Clock));  // open: clr
  Register #(.width(32)) Reg13 (.D(WrData), .en(WrReg13), .Q(RegData13), .clk(Clock));  // open: clr
  Register #(.width(32)) Reg17 (.D(WrData), .en(WrReg17), .Q(RegData17), .clk(Clock));  // open: clr
  Register #(.width(32)) Reg21 (.D(WrData), .en(WrReg21), .Q(RegData21), .clk(Clock));  // open: clr
  Register #(.width(32)) Reg25 (.D(WrData), .en(WrReg25), .Q(RegData25), .clk(Clock));  // open: clr
  Register #(.width(32)) Reg29 (.D(WrData), .en(WrReg29), .Q(RegData29), .clk(Clock));  // open: clr
  Register #(.width(32)) Reg2 (.D(WrData), .en(WrReg2), .Q(RegData2), .clk(Clock));  // open: clr
  Register #(.width(32)) Reg6 (.D(WrData), .en(WrReg6), .Q(RegData6), .clk(Clock));  // open: clr
  Register #(.width(32)) Reg10 (.D(WrData), .en(WrReg10), .Q(RegData10), .clk(Clock));  // open: clr
  Register #(.width(32)) Reg14 (.D(WrData), .en(WrReg14), .Q(RegData14), .clk(Clock));  // open: clr
  Register #(.width(32)) Reg18 (.D(WrData), .en(WrReg18), .Q(RegData18), .clk(Clock));  // open: clr
  Register #(.width(32)) Reg22 (.D(WrData), .en(WrReg22), .Q(RegData22), .clk(Clock));  // open: clr
  Register #(.width(32)) Reg26 (.D(WrData), .en(WrReg26), .Q(RegData26), .clk(Clock));  // open: clr
  Register #(.width(32)) Reg30 (.D(WrData), .en(WrReg30), .Q(RegData30), .clk(Clock));  // open: clr
  Register #(.width(32)) Reg3 (.D(WrData), .en(WrReg3), .Q(RegData3), .clk(Clock));  // open: clr
  Register #(.width(32)) Reg7 (.D(WrData), .en(WrReg7), .Q(RegData7), .clk(Clock));  // open: clr
  Register #(.width(32)) Reg11 (.D(WrData), .en(WrReg11), .Q(RegData11), .clk(Clock));  // open: clr
  Register #(.width(32)) Reg15 (.D(WrData), .en(WrReg15), .Q(RegData15), .clk(Clock));  // open: clr
  Register #(.width(32)) Reg19 (.D(WrData), .en(WrReg19), .Q(RegData19), .clk(Clock));  // open: clr
  Register #(.width(32)) Reg23 (.D(WrData), .en(WrReg23), .Q(RegData23), .clk(Clock));  // open: clr
  Register #(.width(32)) Reg27 (.D(WrData), .en(WrReg27), .Q(RegData27), .clk(Clock));  // open: clr
  Register #(.width(32)) Reg31 (.D(WrData), .en(WrReg31), .Q(RegData31), .clk(Clock));  // open: clr
  Multiplexer #(.select(5), .width(32), .enable("false")) multiplexer_1 (
    .in0({32{1'b0}}), .in1(RegData1), .in2(RegData2), .in3(RegData3), .in4(RegData4), .in5(RegData5),
    .in6(RegData6), .in7(RegData7), .in8(RegData8), .in9(RegData9), .in10(RegData10), .in11(RegData11),
    .in12(RegData12), .in13(RegData13), .in14(RegData14), .in15(RegData15), .in16(RegData16),
    .in17(RegData17), .in18(RegData18), .in19(RegData19), .in20(RegData20), .in21(RegData21),
    .in22(RegData22), .in23(RegData23), .in24(RegData24), .in25(RegData25), .in26(RegData26),
    .in27(RegData27), .in28(RegData28), .in29(RegData29), .in30(RegData30), .in31(RegData31),
    .out(multiplexer_1_out), .sel(RdAddr1));
  Multiplexer #(.select(5), .width(32), .enable("false")) multiplexer_2 (
    .in0({32{1'b0}}), .in1(RegData1), .in2(RegData2), .in3(RegData3), .in4(RegData4), .in5(RegData5),
    .in6(RegData6), .in7(RegData7), .in8(RegData8), .in9(RegData9), .in10(RegData10), .in11(RegData11),
    .in12(RegData12), .in13(RegData13), .in14(RegData14), .in15(RegData15), .in16(RegData16),
    .in17(RegData17), .in18(RegData18), .in19(RegData19), .in20(RegData20), .in21(RegData21),
    .in22(RegData22), .in23(RegData23), .in24(RegData24), .in25(RegData25), .in26(RegData26),
    .in27(RegData27), .in28(RegData28), .in29(RegData29), .in30(RegData30), .in31(RegData31),
    .out(multiplexer_2_out), .sel(RdAddr2));
  Multiplexer #(.width(32), .enable("false")) multiplexer_3 (
    .in0(multiplexer_1_out), .in1(WrData), .out(RdData1), .sel(and_1_out));
  Multiplexer #(.width(32), .enable("false")) multiplexer_4 (
    .in0(multiplexer_2_out), .in1(WrData), .out(RdData2), .sel(and_2_out));
  Comparator #(.width(5), .mode("unsigned")) comparator_1 (
    .a(WrAddr), .b(RdAddr1), .eq(comparator_1_eq));  // open: gt, lt
  and and_1 (and_1_out, comparator_1_eq, WrReg, not_1_out);
  Comparator #(.width(5), .mode("unsigned")) comparator_2 (
    .a(WrAddr), .b(RdAddr2), .eq(comparator_2_eq));  // open: gt, lt
  and and_2 (and_2_out, comparator_2_eq, WrReg, not_2_out);
  Comparator #(.width(5), .mode("unsigned")) comparator_3 (
    .a(WrAddr), .b({5{1'b0}}), .eq(comparator_3_eq));  // open: gt, lt
  not not_1 (not_1_out, comparator_3_eq);
  Comparator #(.width(5), .mode("unsigned")) comparator_4 (
    .a(WrAddr), .b({5{1'b0}}), .eq(comparator_4_eq));  // open: gt, lt
  not not_2 (not_2_out, comparator_4_eq);
endmodule

module Overflow_Unit (
  input  Add,
  input  Sub,
  input  ASign,
  input  BSign,
  input  ResultSign,
  output Overflow
);

  wire and_1_out, and_2_out, or_1_out, xnor_1_out, xor_1_out, xor_2_out;

  xnor xnor_1 (xnor_1_out, ASign, BSign);
  xor xor_1 (xor_1_out, ASign, BSign);
  and and_1 (and_1_out, xnor_1_out, Add);
  and and_2 (and_2_out, xor_1_out, Sub);
  or or_1 (or_1_out, and_1_out, and_2_out);
  xor xor_2 (xor_2_out, ResultSign, ASign);
  and and_3 (Overflow, or_1_out, xor_2_out);

  // Notes on the sheet:
  //   Overflow occurs when doing addition and sign(A) == sign(B) && sign(result) != sign(A)
  //   Or
  //   Overflow occurs when doing subtraction and sign(A) != sign(B) && sign(result) != sign(A)
endmodule

// Fetch Reg
module FetchReg (
  input  Clock,
  input  [31:0] InInst,
  input  [31:0] InPC,
  input  clear,
  input  Stall,
  output [31:0] OutInst,
  output [31:0] OutPC
);

  wire not_1_out, or_1_out;
  wire [31:0] multiplexer_1_out;

  or or_1 (or_1_out, clear, Stall);
  Multiplexer #(.width(32), .enable("false")) multiplexer_1 (
    .in0(InInst), .in1({32{1'b0}}), .out(multiplexer_1_out), .sel(or_1_out));
  not not_1 (not_1_out, or_1_out);
  Register #(.width(32)) Instruction (.D(multiplexer_1_out), .Q(OutInst), .clk(Clock));  // open: en, clr
  Register #(.width(32)) Next_PC (.D(InPC), .en(not_1_out), .Q(OutPC), .clk(Clock));  // open: clr
endmodule

module Decode_Reg (
  input  clock,
  input  [1:0] WrtCtrl,
  input  MemCtrl,
  input  [4:0] ExeCtrl,
  input  [31:0] Read_Data_1,
  input  [31:0] Read_Data_2,
  input  [31:0] Immediate,
  input  [4:0] Source,
  input  [4:0] Target,
  input  [4:0] Dest,
  input  [4:0] Shamt,
  input  clear,
  output [1:0] WrtOut,
  output MemOut,
  output [4:0] ExeOut,
  output [31:0] RD1Out,
  output [31:0] RD2Out,
  output [31:0] ImmOut,
  output [4:0] SrcOut,
  output [4:0] TgtOut,
  output [4:0] DestOut,
  output [4:0] ShamtOut
);

  wire not_1_out, not_2_out, not_3_out, not_4_out, not_5_out, not_6_out, not_7_out, not_8_out, not_9_out,
       not_10_out;

  Register #(.width(2)) register_1 (.D(WrtCtrl), .en(not_1_out), .Q(WrtOut), .clk(clock), .clr(clear));
  not not_1 (not_1_out, clear);
  Register #(.width(1)) register_2 (.D(MemCtrl), .en(not_2_out), .Q(MemOut), .clk(clock), .clr(clear));
  not not_2 (not_2_out, clear);
  Register #(.width(5)) register_3 (.D(ExeCtrl), .en(not_3_out), .Q(ExeOut), .clk(clock), .clr(clear));
  not not_3 (not_3_out, clear);
  Register #(.width(32)) register_4 (.D(Read_Data_1), .en(not_4_out), .Q(RD1Out), .clk(clock), .clr(clear));
  not not_4 (not_4_out, clear);
  Register #(.width(32)) register_5 (.D(Read_Data_2), .en(not_5_out), .Q(RD2Out), .clk(clock), .clr(clear));
  not not_5 (not_5_out, clear);
  Register #(.width(32)) register_6 (.D(Immediate), .en(not_6_out), .Q(ImmOut), .clk(clock), .clr(clear));
  not not_6 (not_6_out, clear);
  Register #(.width(5)) register_7 (.D(Source), .en(not_7_out), .Q(SrcOut), .clk(clock), .clr(clear));
  not not_7 (not_7_out, clear);
  Register #(.width(5)) register_8 (.D(Target), .en(not_8_out), .Q(TgtOut), .clk(clock), .clr(clear));
  not not_8 (not_8_out, clear);
  Register #(.width(5)) register_9 (.D(Dest), .en(not_9_out), .Q(DestOut), .clk(clock), .clr(clear));
  not not_9 (not_9_out, clear);
  Register #(.width(5)) register_10 (.D(Shamt), .en(not_10_out), .Q(ShamtOut), .clk(clock), .clr(clear));
  not not_10 (not_10_out, clear);
endmodule

// Execute REg
module Execute_Reg (
  input  clock,
  input  [1:0] Writeback,
  input  Memory,
  input  [31:0] AluOut,
  input  [31:0] WriteData,
  input  [4:0] WriteReg,
  output [1:0] WriteBack_2,
  output Memory_2,
  output [31:0] AluOut_2,
  output [31:0] WriteData_2,
  output [4:0] WriteReg_2
);

  Register #(.width(2)) WritebackInst (.D(Writeback), .Q(WriteBack_2), .clk(clock));  // open: en, clr
  Register #(.width(1)) MemInst (.D(Memory), .Q(Memory_2), .clk(clock));  // open: en, clr
  Register #(.width(32)) u_AluOut (.D(AluOut), .Q(AluOut_2), .clk(clock));  // open: en, clr
  Register #(.width(32)) u_WriteData (.D(WriteData), .Q(WriteData_2), .clk(clock));  // open: en, clr
  Register #(.width(5)) u_WriteReg (.D(WriteReg), .Q(WriteReg_2), .clk(clock));  // open: en, clr
endmodule

module Mem_Reg (
  input  clock,
  input  [1:0] Writeback,
  input  [31:0] ReadData,
  input  [31:0] AluOut,
  input  [4:0] WriteReg,
  output [1:0] WriteBack_2,
  output [31:0] ReadData_2,
  output [31:0] AluOut_2,
  output [4:0] WriteReg_2
);

  Register #(.width(2)) WritebackInst (.D(Writeback), .Q(WriteBack_2), .clk(clock));  // open: en, clr
  Register #(.width(32)) u_ReadData (.D(ReadData), .Q(ReadData_2), .clk(clock));  // open: en, clr
  Register #(.width(32)) u_AluOut (.D(AluOut), .Q(AluOut_2), .clk(clock));  // open: en, clr
  Register #(.width(5)) u_WriteReg (.D(WriteReg), .Q(WriteReg_2), .clk(clock));  // open: en, clr
endmodule

module Control (
  input  [5:0] Op,
  input  [5:0] Func,
  output [1:0] WR,
  output MM,
  output [4:0] EX,
  output Jal,
  output Branch,
  output Jump
);

  wire nor_1_out;
  wire [7:0] rom_1_data, rom_2_data;

  ALU_ctrl ALUCtrl (.OPC(Op), .Func(Func), .out_3(EX[2:0]));
  ROM #(.addrWidth(6)) rom_1 (.addr(Op), .data(rom_1_data));  // open: sel
  ROM #(.addrWidth(6)) rom_2 (.addr(Func), .data(rom_2_data));  // open: sel
  nor nor_1 (nor_1_out, Op[2], Op[0], Op[1], Op[3], Op[4], Op[5]);
  Multiplexer #(.width(8), .enable("false")) multiplexer_1 (
    .in0(rom_1_data), .in1(rom_2_data), .out({Jump, Branch, Jal, EX[3], EX[4], MM, WR[0], WR[1]}),
    .sel(nor_1_out));

  // Notes on the sheet:
  //   contents of rom_1 (hex, n*v repeats v):
  //   0 0 81 a2 40 0 0 0 13 0 0 0 13 13 21*0 12 7*0 14
  //   contents of rom_2 (hex, n*v repeats v):
  //   b 0 b 5*0 81 23*0 b 0 b 0 b b b 0 0 0 b
endmodule

module ALU_ctrl (
  input  [5:0] OPC,
  input  [5:0] Func,
  output [2:0] out_3
);

  wire and_1_out, and_2_out, and_3_out, and_4_out, and_5_out, and_6_out, and_7_out, and_8_out, and_9_out,
       and_10_out, and_11_out, and_12_out, and_13_out, and_14_out, and_15_out, and_16_out, nor_1_out;
  wire [1:0] or_1_out;
  wire [2:0] or_3_out;

  and and_1 (and_1_out, Func[5], ~Func[2], ~Func[3]);  // AND_Gate
  and and_2 (and_2_out, Func[5], ~Func[3], Func[1]);  // AND_Gate
  and and_3 (and_3_out, ~Func[5], ~Func[1]);  // AND_Gate
  and and_4 (and_4_out, ~Func[5], ~Func[3], ~Func[1]);  // AND_Gate
  and and_5 (and_5_out, Func[1], ~Func[2], ~Func[3]);  // AND_Gate
  and and_6 (and_6_out, Func[5], Func[0]);
  and and_7 (and_7_out, ~Func[0], Func[1], Func[3]);  // AND_Gate
  and and_8 (and_8_out, ~Func[0], Func[1], Func[2]);  // AND_Gate
  and and_9 (and_9_out, ~Func[0], ~Func[3], ~Func[5]);  // AND_Gate
  and and_10 (and_10_out, OPC[3], ~OPC[2]);  // AND_Gate
  and and_11 (and_11_out, OPC[1], ~OPC[2]);  // AND_Gate
  and and_12 (and_12_out, OPC[2], ~OPC[3]);  // AND_Gate
  and and_13 (and_13_out, OPC[5], ~OPC[3]);  // AND_Gate
  and and_14 (and_14_out, OPC[3], OPC[5]);
  and and_15 (and_15_out, ~OPC[1], ~OPC[3]);  // AND_Gate
  and and_16 (and_16_out, OPC[0], ~OPC[1]);  // AND_Gate
  or or_1 (or_1_out[0], and_10_out, and_11_out, and_12_out, and_13_out, and_14_out);
  or or_2 (or_1_out[1], and_15_out, and_16_out);
  or or_3 (or_3_out[0], and_1_out, and_2_out, and_3_out);
  or or_4 (or_3_out[1], and_4_out, and_5_out, and_6_out);
  or or_5 (or_3_out[2], and_7_out, and_8_out, and_9_out);
  nor nor_1 (nor_1_out, OPC[5], OPC[4], OPC[3], OPC[1], OPC[0], OPC[2]);
  Multiplexer #(.width(3), .enable("false")) multiplexer_1 (
    .in0({1'b0, or_1_out}), .in1(or_3_out), .out(out_3), .sel(nor_1_out));
endmodule

module HazardU (
  input  [4:0] WriteRegW,
  input  BranchD,
  input  JumpD,
  input  [4:0] RegSrcD,
  input  [4:0] RegTargetD,
  input  [4:0] RegSrcE,
  input  [4:0] RegTargetE,
  input  [4:0] WriteRegM,
  input  [4:0] WriteRegE,
  input  RegWriteE,
  input  RegWriteM,
  input  MemtoRegM,
  input  RegWriteW,
  input  MemtoRegE,
  output [1:0] ForwardBE,
  output [1:0] ForwardAE,
  output StallF,
  output StallD,
  output ForwardAD,
  output ForwardBD,
  output FlushE
);

  wire comparator_1_eq, comparator_2_eq, comparator_3_eq, comparator_4_eq, comparator_5_eq, comparator_6_eq,
       comparator_7_eq, comparator_8_eq, comparator_9_eq, comparator_10_eq, comparator_11_eq,
       comparator_12_eq, not_2_out, not_3_out, not_4_out, not_5_out, not_6_out, not_7_out, Stall;

  not not_1 (StallF, FlushE);
  and and_1 (FlushE, MemtoRegE, Stall);
  Comparator #(.width(5)) comparator_1 (.a(RegTargetE), .b(RegSrcD), .eq(comparator_1_eq));  // open: gt, lt
  or or_1 (Stall, comparator_1_eq, comparator_2_eq);
  Comparator #(.width(5)) comparator_2 (.a(RegTargetE), .b(RegTargetD), .eq(comparator_2_eq));  // open: gt, lt
  Comparator #(.width(5)) comparator_3 (.a(WriteRegM), .b({5{1'b0}}), .eq(comparator_3_eq));  // open: gt, lt
  Comparator #(.width(5)) comparator_4 (.a(WriteRegM), .b(RegSrcE), .eq(comparator_4_eq));  // open: gt, lt
  Comparator #(.width(5)) comparator_5 (.a(WriteRegW), .b({5{1'b0}}), .eq(comparator_5_eq));  // open: gt, lt
  Comparator #(.width(5)) comparator_6 (.a(WriteRegW), .b(RegSrcE), .eq(comparator_6_eq));  // open: gt, lt
  Comparator #(.width(5)) comparator_7 (.a(WriteRegM), .b(RegSrcE), .eq(comparator_7_eq));  // open: gt, lt
  Comparator #(.width(5)) comparator_8 (.a(WriteRegM), .b({5{1'b0}}), .eq(comparator_8_eq));  // open: gt, lt
  Comparator #(.width(5)) comparator_9 (.a(WriteRegM), .b(RegTargetE), .eq(comparator_9_eq));  // open: gt, lt
  Comparator #(.width(5)) comparator_10 (.a(WriteRegW), .b({5{1'b0}}), .eq(comparator_10_eq));  // open: gt, lt
  Comparator #(.width(5)) comparator_11 (.a(WriteRegW), .b(RegTargetE), .eq(comparator_11_eq));  // open: gt, lt
  Comparator #(.width(5)) comparator_12 (.a(WriteRegM), .b(RegTargetE), .eq(comparator_12_eq));  // open: gt, lt
  not not_2 (not_2_out, comparator_3_eq);
  not not_3 (not_3_out, comparator_5_eq);
  not not_4 (not_4_out, comparator_7_eq);
  not not_5 (not_5_out, comparator_8_eq);
  not not_6 (not_6_out, comparator_10_eq);
  not not_7 (not_7_out, comparator_12_eq);
  and and_2 (ForwardAE[0], not_2_out, RegWriteM, comparator_4_eq);
  and and_3 (ForwardAE[1], not_3_out, RegWriteW, comparator_6_eq, not_4_out);
  and and_4 (ForwardBE[0], not_5_out, RegWriteM, comparator_9_eq);
  and and_5 (ForwardBE[1], not_6_out, RegWriteW, comparator_11_eq, not_7_out);

  assign StallD = FlushE;

  // Other names for the same wires on the sheet: RdM[4:0] = WriteRegM; RdW[4:0] = WriteRegW; RegWriteE_M = RegWriteM;
  //   RegWriteM_W = RegWriteW; RsE[4:0] = RegSrcE; RtE[4:0] = RegTargetE; Y_NStall = FlushE
endmodule
