// Logisim project SingleCycleMips.circ as structural Verilog: 7 circuits, main circuit Main
module Main (
);

  wire alu_1_zero, ALUSrc, and_2_out, Branch, Clock, comparator_1_eq, comparator_2_eq, comparator_3_eq, JRR,
       Jump, MemRead, MemWrite, RegWrite;
  wire [1:0] ALUOp, MemtoReg, RegDst;
  wire [2:0] alucontrol_1_out;
  wire [4:0] WriteAddr;
  wire [5:0] _0_5, OPC;
  wire [7:0] alu_1_aluresult;
  wire [25:6] rom_1_data;
  wire [27:0] bit_extender_1_out, shifter_1_out;
  wire [31:0] adder_2_out, bit_extender_2_out, JR, multiplexer_2_out, multiplexer_3_out, multiplexer_4_out,
       PC, PC_4_32, ram_1_data, RAMData, register_1_q, shifter_2_out, Write;
  wire [31:8] alu_1_aluresult_2;

  Clock clock_1 (.out(Clock));
  Register #(.width(32)) register_1 (.D(PC), .Q(register_1_q), .clk(Clock));  // open: en, clr
  // Probe on register_1_q[7:0]
  Adder #(.width(32)) adder_1 (.a(32'h4), .b(register_1_q), .out(PC_4_32));  // open: cin, cout
  ROM #(.dataWidth(32)) rom_1 (.addr(register_1_q[9:2]), .data({OPC, rom_1_data, _0_5}));  // open: sel
  assign bit_extender_1_out = {{2{1'b0}}, {rom_1_data, _0_5}};  // Bit_Extender bit_extender_1
  // Probe on Jump
  Control control_1 (
    .in_1(OPC), .RegDest(RegDst), .Jump(Jump), .Branch(Branch), .MemRead(MemRead), .MemtoReg(MemtoReg),
    .ALUop(ALUOp), .MemWrite(MemWrite), .ALUsrc(ALUSrc), .RegWrite(RegWrite));
  Multiplexer #(.select(2), .width(5), .enable("false")) multiplexer_1 (
    .in0(rom_1_data[20:16]), .in1(rom_1_data[15:11]), .in2({5{1'b1}}), .out(WriteAddr), .sel(RegDst));  // open: in3
  Comparator #(.width(6)) comparator_1 (.a(6'b000011), .b(OPC), .eq(comparator_1_eq));  // open: gt, lt
  Shifter #(.width(28)) shifter_1 (.in(bit_extender_1_out), .\dist (5'b00010), .out(shifter_1_out));
  // Probe on MemWrite
  // Probe on RegWrite
  // Probe on comparator_1_eq
  // Probe on WriteAddr
  assign bit_extender_2_out = {{16{rom_1_data[15]}}, {rom_1_data[15:6], _0_5}};  // Bit_Extender bit_extender_2
  Register_File register_file_1 (
    .WrAddr(WriteAddr), .WrData(Write), .WrReg(RegWrite), .RdAddr1(rom_1_data[25:21]),
    .RdAddr2(rom_1_data[20:16]), .RdData1(JR), .RdData2(RAMData), .Clock(Clock));
  Multiplexer #(.width(32), .enable("false")) multiplexer_2 (
    .in0(RAMData), .in1(bit_extender_2_out), .out(multiplexer_2_out), .sel(ALUSrc));
  Comparator #(.width(6)) comparator_2 (.a({6{1'b0}}), .b(OPC), .eq(comparator_2_eq));  // open: gt, lt
  and and_1 (JRR, comparator_2_eq, comparator_3_eq);
  Comparator #(.width(6)) comparator_3 (.a(6'b001000), .b(_0_5), .eq(comparator_3_eq));  // open: gt, lt
  Shifter #(.width(32)) shifter_2 (.in(bit_extender_2_out), .\dist (5'b00010), .out(shifter_2_out));
  // Probe on JRR
  Adder #(.width(32)) adder_2 (.a(PC_4_32), .b(shifter_2_out), .out(adder_2_out));  // open: cin, cout
  ALUControl alucontrol_1 (.Control(ALUOp), .OPc(OPC), ._5_0(_0_5), .OUT(alucontrol_1_out));
  ALU alu_1 (
    .ALUCtl(alucontrol_1_out), .A(JR), .B(multiplexer_2_out),
    .ALUResult({alu_1_aluresult_2, alu_1_aluresult}), .Zero(alu_1_zero));  // open: Overflow, Shamt
  // Probe on RAMData[7:0]
  // Probe on Branch
  and and_2 (and_2_out, Branch, alu_1_zero);
  Multiplexer #(.width(32), .enable("false")) multiplexer_3 (
    .in0(PC_4_32), .in1(adder_2_out), .out(multiplexer_3_out), .sel(and_2_out));
  Multiplexer #(.width(32), .enable("false")) multiplexer_4 (
    .in0(multiplexer_3_out), .in1({PC_4_32[31:28], shifter_1_out}), .out(multiplexer_4_out), .sel(Jump));
  RAM #(.dataWidth(32), .bus("separate")) ram_1 (
    .addr(alu_1_aluresult), .din(RAMData), .data(ram_1_data), .str(MemWrite), .clk(Clock), .ld(MemRead));  // open: sel, clr
  Multiplexer #(.width(32), .enable("false")) multiplexer_5 (.in0(multiplexer_4_out), .in1(JR), .out(PC), .sel(JRR));
  Multiplexer #(.select(2), .width(32), .enable("false")) multiplexer_6 (
    .in0({alu_1_aluresult_2, alu_1_aluresult}), .in1(ram_1_data), .in2(PC_4_32), .out(Write), .sel(MemtoReg));  // open: in3
  // Probe on Write[7:0]

  // Notes on the sheet:
  //   contents of rom_1 (hex, n*v repeats v):
  //   20010008 34220005 3043ffff 612020 832822 223024 c33826 aca40064 8ca80064 22482a 1265025 c00000d
  //   200b0001 23ff0018 10c00003 a13022 800000e 200c0001 3e00008 200d0001 200e0001
endmodule

module _32_Bit_Adder_Subtractor (
  input  Add_Sub_control,
  input  [31:0] in_2,
  input  [31:0] in_3,
  output [31:0] out_4,
  output carry_out
);

  wire adder_1_cout, subtractor_1_bout;
  wire [31:0] adder_1_out, subtractor_1_out;

  Adder #(.width(32)) adder_1 (.a(in_2), .b(in_3), .out(adder_1_out), .cout(adder_1_cout));  // open: cin
  Subtractor #(.width(32)) subtractor_1 (
    .a(in_2), .b(in_3), .out(subtractor_1_out), .bout(subtractor_1_bout));  // open: bin
  Multiplexer #(.width(32), .enable("false")) multiplexer_1 (
    .in0(adder_1_out), .in1(subtractor_1_out), .out(out_4), .sel(Add_Sub_control));
  Multiplexer #(.enable("false")) multiplexer_2 (
    .in0(adder_1_cout), .in1(subtractor_1_bout), .out(carry_out), .sel(Add_Sub_control));
endmodule

module ALU (
  input  [2:0] ALUCtl,
  input  [31:0] A,
  input  [31:0] B,
  input  [4:0] Shamt,
  output [31:0] ALUResult,
  output Zero,
  output Overflow
);

  wire and_2_out, and_3_out, comparator_1_lt, not_1_out, not_2_out, or_2_out;
  wire [31:0] Add, And, LessThan, Nor, Or, ShiftLeft, ShiftRight, Sub, Xor;

  // Probe on ALUCtl
  assign Nor = ~(A | B);  // NOR_Gate nor_1, 32 bits wide
  Adder #(.width(32)) adder_1 (.a(A), .b(B), .out(Add));  // open: cin, cout
  Subtractor #(.width(32)) subtractor_1 (.a(A), .b(B), .out(Sub));  // open: bin, bout
  assign And = A & B;  // AND_Gate and_1, 32 bits wide
  assign Or = A | B;  // OR_Gate or_1, 32 bits wide
  assign Xor = A ^ B;  // XOR_Gate xor_1, 32 bits wide
  Comparator #(.width(32)) comparator_1 (.a(A), .b(B), .lt(comparator_1_lt));  // open: gt, eq
  assign LessThan = {{31{1'b0}}, comparator_1_lt};  // Bit_Extender bit_extender_1
  Shifter #(.width(32)) shifter_1 (.in(B), .\dist (Shamt), .out(ShiftLeft));
  Shifter #(.width(32), .shift("lr")) shifter_2 (.in(B), .\dist (Shamt), .out(ShiftRight));
  Multiplexer #(.select(3), .width(32), .enable("false")) multiplexer_1 (
    .in0(And), .in1(Add), .in2(Or), .in3(Sub), .in4(LessThan), .in5(Xor), .in6(ShiftLeft), .in7(ShiftRight),
    .out(ALUResult), .sel(ALUCtl));
  not not_1 (not_1_out, ALUCtl[1]);
  not not_2 (not_2_out, ALUCtl[2]);
  and and_2 (and_2_out, ALUCtl[0], not_1_out, not_2_out);
  and and_3 (and_3_out, ALUCtl[0], ALUCtl[1], not_2_out);
  Overflow_Unit overflow_unit_1 (
    .Add(and_2_out), .Sub(and_3_out), .ASign(A[31]), .BSign(B[31]), .ResultSign(ALUResult[31]),
    .Overflow(Overflow));
  or or_2 (or_2_out, ALUResult[0], ALUResult[1], ALUResult[2], ALUResult[3], ALUResult[4], ALUResult[5], ALUResult[6], ALUResult[7], ALUResult[8], ALUResult[9], ALUResult[10], ALUResult[11], ALUResult[12], ALUResult[13], ALUResult[14], ALUResult[15], ALUResult[16], ALUResult[17], ALUResult[18], ALUResult[19], ALUResult[20], ALUResult[21], ALUResult[22], ALUResult[23], ALUResult[24], ALUResult[25], ALUResult[26], ALUResult[27], ALUResult[28], ALUResult[29], ALUResult[30], ALUResult[31]);
  not not_3 (Zero, or_2_out);

  // Other names for the same wires on the sheet: ASign = A[31]; ResultSign = ALUResult[31]; BSign = B[31]
endmodule

module Register_File (
  input  [4:0] WrAddr,
  input  [31:0] WrData,
  input  WrReg,
  input  [4:0] RdAddr1,
  input  [4:0] RdAddr2,
  input  Clock,
  output [31:0] RdData1,
  output [31:0] RdData2
);

  wire WrReg0, WrReg1, WrReg2, WrReg3, WrReg4, WrReg5, WrReg6, WrReg7, WrReg8, WrReg9, WrReg10, WrReg11,
       WrReg12, WrReg13, WrReg14, WrReg15, WrReg16, WrReg17, WrReg18, WrReg19, WrReg20, WrReg21, WrReg22,
       WrReg23, WrReg24, WrReg25, WrReg26, WrReg27, WrReg28, WrReg29, WrReg30, WrReg31;
  wire [31:0] RegData1, RegData2, RegData3, RegData4, RegData5, RegData6, RegData7, RegData8, RegData9,
       RegData10, RegData11, RegData12, RegData13, RegData14, RegData15, RegData16, RegData17, RegData18,
       RegData19, RegData20, RegData21, RegData22, RegData23, RegData24, RegData25, RegData26, RegData27,
       RegData28, RegData29, RegData30, RegData31;

  Demultiplexer #(.select(5), .enable("false")) demultiplexer_1 (
    .out0(WrReg0), .out1(WrReg1), .out2(WrReg2), .out3(WrReg3), .out4(WrReg4), .out5(WrReg5), .out6(WrReg6),
    .out7(WrReg7), .out8(WrReg8), .out9(WrReg9), .out10(WrReg10), .out11(WrReg11), .out12(WrReg12),
    .out13(WrReg13), .out14(WrReg14), .out15(WrReg15), .out16(WrReg16), .out17(WrReg17), .out18(WrReg18),
    .out19(WrReg19), .out20(WrReg20), .out21(WrReg21), .out22(WrReg22), .out23(WrReg23), .out24(WrReg24),
    .out25(WrReg25), .out26(WrReg26), .out27(WrReg27), .out28(WrReg28), .out29(WrReg29), .out30(WrReg30),
    .out31(WrReg31), .in(WrReg), .sel(WrAddr));
  Register #(.width(32)) Reg4 (.D(WrData), .en(WrReg4), .Q(RegData4), .clk(Clock));  // open: clr
  Register #(.width(32)) Reg8 (.D(WrData), .en(WrReg8), .Q(RegData8), .clk(Clock));  // open: clr
  Register #(.width(32)) Reg12 (.D(WrData), .en(WrReg12), .Q(RegData12), .clk(Clock));  // open: clr
  Register #(.width(32)) Reg16 (.D(WrData), .en(WrReg16), .Q(RegData16), .clk(Clock));  // open: clr
  Register #(.width(32)) Reg20 (.D(WrData), .en(WrReg20), .Q(RegData20), .clk(Clock));  // open: clr
  Register #(.width(32)) Reg24 (.D(WrData), .en(WrReg24), .Q(RegData24), .clk(Clock));  // open: clr
  Register #(.width(32)) Reg28 (.D(WrData), .en(WrReg28), .Q(RegData28), .clk(Clock));  // open: clr
  Register #(.width(32)) Reg1 (.D(WrData), .en(WrReg1), .Q(RegData1), .clk(Clock));  // open: clr
  Register #(.width(32)) Reg5 (.D(WrData), .en(WrReg5), .Q(RegData5), .clk(Clock));  // open: clr
  Register #(.width(32)) Reg9 (.D(WrData), .en(WrReg9), .Q(RegData9), .clk(Clock));  // open: clr
  Register #(.width(32)) Reg13 (.D(WrData), .en(WrReg13), .Q(RegData13), .clk(Clock));  // open: clr
  Register #(.width(32)) Reg17 (.D(WrData), .en(WrReg17), .Q(RegData17), .clk(Clock));  // open: clr
  Register #(.width(32)) Reg21 (.D(WrData), .en(WrReg21), .Q(RegData21), .clk(Clock));  // open: clr
  Register #(.width(32)) Reg25 (.D(WrData), .en(WrReg25), .Q(RegData25), .clk(Clock));  // open: clr
  Register #(.width(32)) Reg29 (.D(WrData), .en(WrReg29), .Q(RegData29), .clk(Clock));  // open: clr
  Register #(.width(32)) Reg2 (.D(WrData), .en(WrReg2), .Q(RegData2), .clk(Clock));  // open: clr
  Register #(.width(32)) Reg6 (.D(WrData), .en(WrReg6), .Q(RegData6), .clk(Clock));  // open: clr
  Register #(.width(32)) Reg10 (.D(WrData), .en(WrReg10), .Q(RegData10), .clk(Clock));  // open: clr
  Register #(.width(32)) Reg14 (.D(WrData), .en(WrReg14), .Q(RegData14), .clk(Clock));  // open: clr
  Register #(.width(32)) Reg18 (.D(WrData), .en(WrReg18), .Q(RegData18), .clk(Clock));  // open: clr
  Register #(.width(32)) Reg22 (.D(WrData), .en(WrReg22), .Q(RegData22), .clk(Clock));  // open: clr
  Register #(.width(32)) Reg26 (.D(WrData), .en(WrReg26), .Q(RegData26), .clk(Clock));  // open: clr
  Register #(.width(32)) Reg30 (.D(WrData), .en(WrReg30), .Q(RegData30), .clk(Clock));  // open: clr
  Register #(.width(32)) Reg3 (.D(WrData), .en(WrReg3), .Q(RegData3), .clk(Clock));  // open: clr
  Register #(.width(32)) Reg7 (.D(WrData), .en(WrReg7), .Q(RegData7), .clk(Clock));  // open: clr
  Register #(.width(32)) Reg11 (.D(WrData), .en(WrReg11), .Q(RegData11), .clk(Clock));  // open: clr
  Register #(.width(32)) Reg15 (.D(WrData), .en(WrReg15), .Q(RegData15), .clk(Clock));  // open: clr
  Register #(.width(32)) Reg19 (.D(WrData), .en(WrReg19), .Q(RegData19), .clk(Clock));  // open: clr
  Register #(.width(32)) Reg23 (.D(WrData), .en(WrReg23), .Q(RegData23), .clk(Clock));  // open: clr
  Register #(.width(32)) Reg27 (.D(WrData), .en(WrReg27), .Q(RegData27), .clk(Clock));  // open: clr
  Register #(.width(32)) Reg31 (.D(WrData), .en(WrReg31), .Q(RegData31), .clk(Clock));  // open: clr
  Multiplexer #(.select(5), .width(32), .enable("false")) multiplexer_1 (
    .in0({32{1'b0}}), .in1(RegData1), .in2(RegData2), .in3(RegData3), .in4(RegData4), .in5(RegData5),
    .in6(RegData6), .in7(RegData7), .in8(RegData8), .in9(RegData9), .in10(RegData10), .in11(RegData11),
    .in12(RegData12), .in13(RegData13), .in14(RegData14), .in15(RegData15), .in16(RegData16),
    .in17(RegData17), .in18(RegData18), .in19(RegData19), .in20(RegData20), .in21(RegData21),
    .in22(RegData22), .in23(RegData23), .in24(RegData24), .in25(RegData25), .in26(RegData26),
    .in27(RegData27), .in28(RegData28), .in29(RegData29), .in30(RegData30), .in31(RegData31), .out(RdData1),
    .sel(RdAddr1));
  Multiplexer #(.select(5), .width(32), .enable("false")) multiplexer_2 (
    .in0({32{1'b0}}), .in1(RegData1), .in2(RegData2), .in3(RegData3), .in4(RegData4), .in5(RegData5),
    .in6(RegData6), .in7(RegData7), .in8(RegData8), .in9(RegData9), .in10(RegData10), .in11(RegData11),
    .in12(RegData12), .in13(RegData13), .in14(RegData14), .in15(RegData15), .in16(RegData16),
    .in17(RegData17), .in18(RegData18), .in19(RegData19), .in20(RegData20), .in21(RegData21),
    .in22(RegData22), .in23(RegData23), .in24(RegData24), .in25(RegData25), .in26(RegData26),
    .in27(RegData27), .in28(RegData28), .in29(RegData29), .in30(RegData30), .in31(RegData31), .out(RdData2),
    .sel(RdAddr2));
endmodule

module Overflow_Unit (
  input  Add,
  input  Sub,
  input  ASign,
  input  BSign,
  input  ResultSign,
  output Overflow
);

  wire and_1_out, and_2_out, or_1_out, xnor_1_out, xor_1_out, xor_2_out;

  xnor xnor_1 (xnor_1_out, ASign, BSign);
  xor xor_1 (xor_1_out, ASign, BSign);
  and and_1 (and_1_out, xnor_1_out, Add);
  and and_2 (and_2_out, xor_1_out, Sub);
  or or_1 (or_1_out, and_1_out, and_2_out);
  xor xor_2 (xor_2_out, ResultSign, ASign);
  and and_3 (Overflow, or_1_out, xor_2_out);

  // Notes on the sheet:
  //   Overflow occurs when doing addition and sign(A) == sign(B) && sign(result) != sign(A)
  //   Or
  //   Overflow occurs when doing subtraction and sign(A) != sign(B) && sign(result) != sign(A)
endmodule

module Control (
  input  [5:0] in_1,
  output [1:0] RegDest,
  output Jump,
  output Branch,
  output MemRead,
  output [1:0] MemtoReg,
  output [1:0] ALUop,
  output MemWrite,
  output ALUsrc,
  output RegWrite
);

  ROM #(.addrWidth(6), .dataWidth(12)) rom_1 (
    .addr(in_1), .data({RegWrite, ALUsrc, MemWrite, ALUop, MemtoReg, MemRead, Branch, Jump, RegDest}));  // open: sel

  // Notes on the sheet:
  //   contents of rom_1 (hex, n*v repeats v):
  //   901 0 4 846 88 0 0 0 d00 0 0 0 d00 d00 21*0 c50 7*0 600
endmodule

module ALUControl (
  input  [1:0] Control,
  input  [5:0] OPc,
  input  [5:0] _5_0,
  output [2:0] OUT
);

  wire not_1_out, or_1_out;
  wire [2:0] multiplexer_1_out, rom_1_data, rom_2_data;

  or or_1 (or_1_out, OPc[0], OPc[1], OPc[2], OPc[3], OPc[4], OPc[5]);
  ROM #(.addrWidth(6), .dataWidth(3)) rom_1 (.addr(OPc), .data(rom_1_data));  // open: sel
  ROM #(.addrWidth(6), .dataWidth(3)) rom_2 (.addr(_5_0), .data(rom_2_data));  // open: sel
  not not_1 (not_1_out, or_1_out);
  Multiplexer #(.width(3), .enable("false")) multiplexer_1 (
    .in0(rom_1_data), .in1(rom_2_data), .out(multiplexer_1_out), .sel(not_1_out));
  Multiplexer #(.select(2), .width(3), .enable("false")) multiplexer_2 (
    .in0(3'b001), .in1(3'b011), .in2(multiplexer_1_out), .out(OUT), .sel(Control));  // open: in3

  // Notes on the sheet:
  //   contents of rom_1 (hex, n*v repeats v):
  //   8*0 1 4*0 2
  //   contents of rom_2 (hex, n*v repeats v):
  //   8*0 2 23*0 1 0 3 0 0 2 5 0 0 0 4
endmodule
